# Fritzing sketch Schematic (saved by Fritzing 1.0.2b)
breadboards: 1

parts:
  U1 = Adafruit Feather M0 Adalogger [part_number="Adafruit #2796"]
  U2 = Adafruit 128x64 OLED FeatherWing [part_number="Adafruit #4650"]
  U3 = Adafruit FeatherWing Proto [part_number="Adafruit #2884"]
  R1 = Resistor [tolerance=±5% power=0.25W resistance=47 package=THT]
  Q1 = LTR-301 [mpn=1540031NC6090 mn="Würth Elektronik" package=ltr-301]
  LED1 = LEDs [mpn=IR333-A package=led10mm]
  LED2 = LEDs [mpn=XLUR12D mn=SunLED package=led10mm]
  Q3 = LTR-301 [mpn=BPW85B mn="Vishay Semiconductor Opto Division" package=ltr-301]
  R2 = Resistor [tolerance=±5% power=0.25W resistance=100 package=THT]
  Q2 = LTR-301 [mpn=1540031NC6090 mn="Würth Elektronik" package=ltr-301]
  Q4 = LTR-301 [mpn=BPW85B mn="Vishay Semiconductor Opto Division" package=ltr-301]
  Q5 = NPN-Transistor [mpn=bc337-40 mn=NXP package="TO92 [THT]"]
  Q6 = NPN-Transistor [mpn=bc337-40 mn=NXP package="TO92 [THT]"]
  R3 = Resistor [tolerance=±5% power=0.25W resistance=220 package=THT]
  R4 = Resistor [tolerance=±5% power=0.25W resistance=220 package=THT]
  R5 = Resistor [tolerance=±5% power=0.25W resistance=220 package=THT]
  R6 = Resistor [tolerance=±5% power=0.25W resistance=220 package=THT]
  Q7 = NPN-Transistor [mpn=bc337-40 mn=NXP package="TO92 [THT]"]
  Q8 = NPN-Transistor [mpn=bc337-40 mn=NXP package="TO92 [THT]"]
  R7 = Resistor [tolerance=±5% power=0.25W resistance=220 package=THT]
  R8 = Resistor [tolerance=±5% power=0.25W resistance=220 package=THT]
  Q9 = NPN-Transistor [mpn=bc337-40 mn=NXP package="TO92 [THT]"]
  Q10 = NPN-Transistor [mpn=bc337-40 mn=NXP package="TO92 [THT]"]
  R9 = Resistor [tolerance=±5% power=0.25W resistance=220 package=THT]
  R10 = Resistor [tolerance=±5% power=0.25W resistance=220 package=THT]
  Q11 = NPN-Transistor [mpn=bc337-40 mn=NXP package="TO92 [THT]"]
  Q12 = NPN-Transistor [mpn=bc337-40 mn=NXP package="TO92 [THT]"]

nets:
  GND: U1.GND, U2.GND, U3.GND, R1.Pin_1, R2.Pin_1, Q5.E, Q6.E, Q7.E, Q8.E, Q9.E, Q10.E, Q11.E, Q12.E
  N1: U1.A4, U3.E, R5.Pin_1, Q7.C
  N2: U1.A3, U3.D, R9.Pin_1, Q12.C
  N3: U1.A2, U3.C, Q6.C, R4.Pin_1
  N4: U1.A1, U3.B, R7.Pin_1, Q9.C
  +3V3: U1.+3V3, U2.3.3V, U3.3V, Q1.C, Q3.C, Q2.C, Q4.C, R3.Pin_0, R4.Pin_0, R5.Pin_0, R6.Pin_0, R7.Pin_0, R8.Pin_0, R9.Pin_0, R10.Pin_0
  N5: U1.!RESET, U2.!RESET
  N6: U1.D12, U3.M, LED1.A
  N7: U1.D11, U3.L, LED2.A
  N8: U1.D9, U2.J
  N9: U1.D6, U2.I
  N10: U1.D5, U2.H
  N11: U1.SCL, U2.SCL
  N12: U1.SDA, U2.SDA
  N13: R1.Pin_0, LED2.C
  N14: Q1.E, Q5.B
  N15: LED1.C, R2.Pin_0
  N16: Q3.E, Q10.B
  N17: Q2.E, Q8.B
  N18: Q4.E, Q11.B
  N19: Q5.C, Q6.B, R3.Pin_1
  N20: R6.Pin_1, Q7.B, Q8.C
  N21: R8.Pin_1, Q9.B, Q10.C
  N22: R10.Pin_1, Q11.C, Q12.B

notes:
  Work In Progress, not all values yet determined

custom parts:
  Adafruit Feather M0 Adalogger: This is the Adafruit Feather M0 Adalogger - our take on an 'all-in-one' Cortex M0 datalogger (or data-reader) with built in USB and battery charging. Its an Adafruit Feather M0 with a microSD holder ready to rock! We have other boards in the Feather family, check'em out here At the Feather M0's heart is an ATSAMD21G18 ARM Cortex M0 processor, clocked at 48 MHz and at 3.3V logic, the same one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
  Adafruit 128x64 OLED FeatherWing: A Feather board without ambition is a Feather board without FeatherWings! This is the FeatherWing 128x64 OLED: it adds a gorgeous 128x64 monochrome OLED plus 3 user buttons to any Feather main board. Using our Feather Stacking Headers or Feather Female Headers you can connect a FeatherWing on top of your Feather board and let the board take flight! These displays are small, only about 1.3"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
  Adafruit FeatherWing Proto: This is the FeatherWing Proto - a prototyping add-on for all Feather boards. Using our Feather Stacking Headers or Feather Female Headers you can connect a FeatherWing on top or bottom of your Feather board and let the board take flight! This has a duplicate breakout for each pin on a Feather, as well as a bunch of plain grid proto holes. For GND and 3.3V, we give you a strip of connected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
